# Fritzing sketch PowerMonitor_Schematics_with_LCD (saved by Fritzing 0.9.3b)
breadboards: 2

parts:
  Bauteil1 = Arduino Nano (Rev3.0)
  Bauteil2 = Adafruit INA219 High Side DC Current Sensor Breakout [part_number="Adafruit #904"]
  J1 = male pin header, 2 pins [form="♂ (male)"]
  LCD1 = LCD screen

nets:
  GND: Bauteil1.GND, Bauteil2.GND, LCD1.VSS
  5V: Bauteil1.5V, Bauteil2.VCC, LCD1.VDD
  N1: Bauteil1.A5, Bauteil2.SCL
  N2: Bauteil1.A4, Bauteil2.SDA
  N3: Bauteil2.VIN-, J1.pin1
  N4: Bauteil2.VIN+, J1.pin2

custom parts:
  Adafruit INA219 High Side DC Current Sensor Breakout: This breakout board will solve all your power-monitoring problems. Instead of struggling with two multimeters, you can just use the handy INA219B chip on this breakout to both measure both the high side voltage and DC current draw over I2C with 1% precision. Most current-measuring devices such as our current panel meter are only good for low side measuring. That means that unless you want to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
